# Fritzing sketch P08_00_00-BatteryTest (saved by Fritzing 0.9.3b)
breadboards: 2

parts:
  Part1 = Arduino Pro Mini v13
  U1 = FS1000A - 433Mhz RF Transmitter [package=THT]
  U2 = RF-LINK_RX [package=rf-link_rx]
  U3 = attiny85 [package=dip]
  U4 = LIPO-1000mAh [package=lipo-1000]

nets:
  GND: Part1.GND, U2.GND
  VCC: Part1.VCC, U2.VCC
  N1: Part1.D9_PWM, U2.Data#3
  N2: U1.DATA, U3.Pin_5
  N3: U1.VCC, U3.Pin_7, U3.Pin_8, U4.+
  N4: U1.GND, U3.Pin_4, U4.-

custom parts:
  FS1000A - 433Mhz RF Transmitter: This is 433Mhz RF transmitter with receiver kit for Arduino ARM MCU wireless Application environment: Remote control switch, receiver module, motorcycles, automobile anti-theft products, home security products, electric doors, shutter doors, windows, remote control socket, remote control LED, remote audio remote control electric doors, garage door remote control, remote control retractable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
  RF-LINK_RX: RF Link receivers- WRL-8947, 8948, 8949, 8950
